// Logisim project pipeline_components.circ as structural Verilog
module ID (
  input  [19:0] in_1,
  input  in_2,
  input  clock,
  output [3:0] Rd,
  output [3:0] Rt,
  output [3:0] Rs,
  output [7:0] Rs_Value,
  output [7:0] Rt_Value,
  output [7:0] Im
);

  wire ctrl_unit_1_alusrc, ctrl_unit_1_regdatasrc, ctrl_unit_1_regdest, ctrl_unit_1_regwrite,
       instruction_splitter_1_jump;
  wire [1:0] ctrl_unit_1_branch_x3b;
  wire [3:0] instruction_splitter_1_op_code, instruction_splitter_1_r_d;
  wire [7:0] undriven;

  Clock clock_1 ();  // open: out
  Instruction_Splitter instruction_splitter_1 (
    .instruction(in_1), .OP_code(instruction_splitter_1_op_code), .R_s(Rs), .R_t(Rt),
    .R_d(instruction_splitter_1_r_d), .Immidiate(Im), .Jump(instruction_splitter_1_jump));
  ctrl_unit ctrl_unit_1 (
    .in_1(instruction_splitter_1_op_code), .Branch_X3b(ctrl_unit_1_branch_x3b),
    .regWrite(ctrl_unit_1_regwrite), .regDataSrc(ctrl_unit_1_regdatasrc), .RegDest(ctrl_unit_1_regdest),
    .ALUsrc(ctrl_unit_1_alusrc));  // open: MemRad, MemWrite
  Multiplexer #(.width(4)) multiplexer_1 (
    .in0(instruction_splitter_1_r_d), .in1(Rt), .out(Rd), .sel(ctrl_unit_1_regdest), .en(1'b1));
  _8bit_8Registor u_8bit_8registor_1 (
    .WriteEnable(ctrl_unit_1_regwrite), .Data(undriven), .Clock(clock), .BusA(Rs_Value), .BusB(Rt_Value),
    .RegD(Rd), .RegB(Rt), .RegA(Rs), .Reset(in_2));
  ALU_ctrl alu_ctrl_1 (.in_1(instruction_splitter_1_op_code));  // open: out_2
endmodule
